// Logisim project ampel.circ as structural Verilog: 1 circuit, main circuit main
module main (
);

  wire and_1_out, and_2_out, and_3_out, and_4_out, and_5_out, button_1_out, clock_1_out, counter_1_q,
       nor_1_out, not_1_out, not_2_out, not_3_out, not_4_out, not_5_out, not_6_out, not_7_out, not_8_out,
       not_9_out, s_r_ff_1_q, s_r_ff_2_q, s_r_ff_3_q;
  wire [3:0] counter_2_q;

  nor nor_1 (nor_1_out, button_1_out, and_5_out);
  Button button_1 (.out(button_1_out));
  Clock clock_1 (.out(clock_1_out));
  Counter #(.width(1), .max('h1)) counter_1 (
    .count(1'b1), .Q(counter_1_q), .clk(nor_1_out));  // open: load, D, carry, clr
  and and_1 (and_1_out, clock_1_out, counter_1_q);
  Counter #(.width(4), .max('hf)) counter_2 (
    .count(1'b1), .Q(counter_2_q), .clk(and_1_out));  // open: load, D, carry, clr
  not not_1 (not_1_out, counter_2_q[0]);
  not not_2 (not_2_out, counter_2_q[1]);
  not not_3 (not_3_out, counter_2_q[2]);
  not not_4 (not_4_out, counter_2_q[3]);
  not not_5 (not_5_out, counter_2_q[1]);
  not not_6 (not_6_out, counter_2_q[3]);
  not not_7 (not_7_out, counter_2_q[0]);
  not not_8 (not_8_out, counter_2_q[1]);
  not not_9 (not_9_out, counter_2_q[2]);
  and and_2 (and_2_out, not_1_out, not_2_out, not_3_out, not_4_out);
  and and_3 (and_3_out, counter_2_q[0], not_5_out, counter_2_q[2], not_6_out);
  and and_4 (and_4_out, not_7_out, not_8_out, not_9_out, counter_2_q[3]);
  and and_5 (and_5_out, counter_2_q[0], counter_2_q[1], counter_2_q[2], counter_2_q[3]);
  S_R_Flip_Flop #(.trigger("high")) s_r_ff_1 (
    .S(and_2_out), .clk(and_1_out), .R(s_r_ff_3_q), .Q(s_r_ff_1_q));  // open: Qn, preset, reset, en
  S_R_Flip_Flop #(.trigger("high")) s_r_ff_2 (
    .S(and_3_out), .clk(and_1_out), .R(s_r_ff_3_q), .Q(s_r_ff_2_q));  // open: Qn, preset, reset, en
  S_R_Flip_Flop #(.trigger("high")) s_r_ff_3 (
    .S(and_4_out), .clk(and_1_out), .R(and_5_out), .Q(s_r_ff_3_q));  // open: Qn, preset, reset, en
  LED led_1 (.in(s_r_ff_1_q));
  LED led_2 (.in(s_r_ff_2_q));
  LED led_3 (.in(s_r_ff_3_q));
endmodule
